// Logisim project connect4_circuit.circ as structural Verilog: 5 circuits, main circuit main
module main (
  input  [48:0] in_1
);

  column_rgb column_rgb_1 (.in_1(in_1[48:42]));
  column_rgb column_rgb_2 (.in_1(in_1[41:35]));
  column_rgb column_rgb_3 (.in_1(in_1[34:28]));
  column_rgb column_rgb_4 (.in_1(in_1[27:21]));
  column_rgb column_rgb_5 (.in_1(in_1[20:14]));
  column_rgb column_rgb_6 (.in_1(in_1[13:7]));
  column_rgb column_rgb_7 (.in_1(in_1[6:0]));
endmodule

module state_decoder (
  input  [48:0] in_1,
  output [13:0] C0,
  output [13:0] C1,
  output [13:0] C2,
  output [13:0] C3,
  output [13:0] C4,
  output [13:0] C5
);
endmodule

module color_decoder (
  input  [1:0] in_1,
  output G,
  output R,
  output B
);

  not not_1 (G, in_1[1]);
  nor nor_1 (B, in_1[1], in_1[0]);

  assign R = 1'b1;

  // Notes on the sheet:
  //   00 - empty
  //   10 - player 1
  //   01 - player 2
endmodule

module column_decoder (
  input  [6:0] I,
  output [1:0] R5,
  output [1:0] R4,
  output [1:0] R3,
  output [1:0] R2,
  output [1:0] R1,
  output [1:0] R0
);

  wire comparator_1_gt, comparator_2_gt, comparator_3_gt, comparator_4_gt, comparator_5_gt, comparator_6_gt,
       not_1_out, not_2_out, not_3_out, not_4_out, not_5_out, not_6_out;
  wire [2:0] priority_encoder_1_out;

  Priority_Encoder priority_encoder_1 (
    .in0(I[0]), .in1(I[1]), .in2(I[2]), .in3(I[3]), .in4(I[4]), .in5(I[5]), .in6(I[6]), .in7(1'b0),
    .out(priority_encoder_1_out), .en_in(1'b1));  // open: gs, en_out
  Comparator #(.mode("unsigned"), .width(3)) comparator_1 (
    .a(priority_encoder_1_out), .b(3'b101), .gt(comparator_1_gt));  // open: eq, lt
  Comparator #(.mode("unsigned"), .width(3)) comparator_2 (
    .a(priority_encoder_1_out), .b(3'b100), .gt(comparator_2_gt));  // open: eq, lt
  Comparator #(.mode("unsigned"), .width(3)) comparator_3 (
    .a(priority_encoder_1_out), .b(3'b011), .gt(comparator_3_gt));  // open: eq, lt
  Comparator #(.mode("unsigned"), .width(3)) comparator_4 (
    .a(priority_encoder_1_out), .b(3'b010), .gt(comparator_4_gt));  // open: eq, lt
  Comparator #(.mode("unsigned"), .width(3)) comparator_5 (
    .a(priority_encoder_1_out), .b(3'b001), .gt(comparator_5_gt));  // open: eq, lt
  Comparator #(.mode("unsigned"), .width(3)) comparator_6 (
    .a(priority_encoder_1_out), .b(3'b000), .gt(comparator_6_gt));  // open: eq, lt
  not not_1 (not_1_out, I[5]);
  not not_2 (not_2_out, I[4]);
  not not_3 (not_3_out, I[3]);
  not not_4 (not_4_out, I[2]);
  not not_5 (not_5_out, I[1]);
  not not_6 (not_6_out, I[0]);
  and and_1 (R5[0], not_1_out, comparator_1_gt);
  and and_2 (R5[1], I[5], comparator_1_gt);
  and and_3 (R4[0], not_2_out, comparator_2_gt);
  and and_4 (R4[1], I[4], comparator_2_gt);
  and and_5 (R3[0], not_3_out, comparator_3_gt);
  and and_6 (R3[1], I[3], comparator_3_gt);
  and and_7 (R2[0], not_4_out, comparator_4_gt);
  and and_8 (R2[1], I[2], comparator_4_gt);
  and and_9 (R1[0], not_5_out, comparator_5_gt);
  and and_10 (R1[1], I[1], comparator_5_gt);
  and and_11 (R0[0], not_6_out, comparator_6_gt);
  and and_12 (R0[1], I[0], comparator_6_gt);
endmodule

module column_rgb (
  input  [6:0] in_1
);

  wire color_decoder_1_b, color_decoder_1_g, color_decoder_1_r, color_decoder_2_b, color_decoder_2_g,
       color_decoder_2_r, color_decoder_3_b, color_decoder_3_g, color_decoder_3_r, color_decoder_4_b,
       color_decoder_4_g, color_decoder_4_r, color_decoder_5_b, color_decoder_5_g, color_decoder_5_r,
       color_decoder_6_b, color_decoder_6_g, color_decoder_6_r;
  wire [1:0] column_decoder_1_r0, column_decoder_1_r1, column_decoder_1_r2, column_decoder_1_r3,
       column_decoder_1_r4, column_decoder_1_r5;

  column_decoder column_decoder_1 (
    .I(in_1), .R5(column_decoder_1_r5), .R4(column_decoder_1_r4), .R3(column_decoder_1_r3),
    .R2(column_decoder_1_r2), .R1(column_decoder_1_r1), .R0(column_decoder_1_r0));
  color_decoder color_decoder_1 (
    .in_1(column_decoder_1_r5), .G(color_decoder_1_g), .R(color_decoder_1_r), .B(color_decoder_1_b));
  // RGBLED rgbled_1: pin names not known; wires that end beside it: color_decoder_1_r, color_decoder_1_g, color_decoder_1_b
  color_decoder color_decoder_2 (
    .in_1(column_decoder_1_r4), .G(color_decoder_2_g), .R(color_decoder_2_r), .B(color_decoder_2_b));
  // RGBLED rgbled_2: pin names not known; wires that end beside it: color_decoder_2_r, color_decoder_2_g, color_decoder_2_b
  color_decoder color_decoder_3 (
    .in_1(column_decoder_1_r3), .G(color_decoder_3_g), .R(color_decoder_3_r), .B(color_decoder_3_b));
  // RGBLED rgbled_3: pin names not known; wires that end beside it: color_decoder_3_r, color_decoder_3_g, color_decoder_3_b
  color_decoder color_decoder_4 (
    .in_1(column_decoder_1_r2), .G(color_decoder_4_g), .R(color_decoder_4_r), .B(color_decoder_4_b));
  // RGBLED rgbled_4: pin names not known; wires that end beside it: color_decoder_4_r, color_decoder_4_g, color_decoder_4_b
  color_decoder color_decoder_5 (
    .in_1(column_decoder_1_r1), .G(color_decoder_5_g), .R(color_decoder_5_r), .B(color_decoder_5_b));
  // RGBLED rgbled_5: pin names not known; wires that end beside it: color_decoder_5_r, color_decoder_5_g, color_decoder_5_b
  color_decoder color_decoder_6 (
    .in_1(column_decoder_1_r0), .G(color_decoder_6_g), .R(color_decoder_6_r), .B(color_decoder_6_b));
  // RGBLED rgbled_6: pin names not known; wires that end beside it: color_decoder_6_r, color_decoder_6_g, color_decoder_6_b
endmodule
